# Fritzing sketch Hardware (saved by Fritzing 0.9.3b)
breadboards: 1

parts:
  Part1 = Arduino Uno (Rev3)
  U1 = RELAY [package=relay-jzc]
  Power_plug1 = Power plug
  L1 = Solenoid
  L3 = Solenoid
  L4 = Solenoid
  U3 = RELAY [package=relay-jzc]
  U4 = RELAY [package=relay-jzc]

nets:
  N1: Part1.D8, U3.COIL1
  N2: Part1.D9_PWM, U1.COIL1
  N3: Part1.D7, U4.COIL1
  N4: Part1.GND, U1.MAIN, U3.MAIN, U4.MAIN
  N5: U1.NC, Power_plug1.VCC
  N6: Power_plug1.GND, L1.pin1, L3.pin1, L4.pin1
  N7: U3.NC, U3.NO, U4.NC
